# Fritzing sketch self_driving_car_schematic (saved by Fritzing 1.0.2b)

parts:
  S1 = H-Bridge with L298N
  Raspberry_Pi_1 = Raspberry Pi 3 [part_number=RPI-3-V1.2]
  M1 = gear-motor
  M2 = gear-motor
  M3 = gear-motor
  M4 = gear-motor
  CAMERA1 = TTL Serial JPEG Camera  # not connected

nets:
  GND: S1.GND, S1.IN4, Raspberry_Pi_1.GND, Raspberry_Pi_1.GPIO24, Raspberry_Pi_1.GPIO14
  N1: S1.ENA, Raspberry_Pi_1.GPIO22, Raspberry_Pi_1.3V3
  N2: S1.IN1, Raspberry_Pi_1.GPIO17
  N3: S1.IN2, Raspberry_Pi_1.GPIO27
  N4: S1.IN3, Raspberry_Pi_1.GPIO23
  N5: S1.ENB, Raspberry_Pi_1.GPIO8, Raspberry_Pi_1.GPIO25
  N6: S1.M1-01, M1.pin_2, M3.pin_2
  N7: S1.M1-02, M1.pin_1, M3.pin_1
  N8: S1.M2-01, M2.pin_2, M4.pin_1
  N9: S1.M2-02, M2.pin_1, M4.pin_2

custom parts:
  H-Bridge with L298N: h-bridge
  TTL Serial JPEG Camera: TTL Serial JPEG Camera with NTSC Out
